# Fritzing sketch interface_circuit (saved by Fritzing 0.9.9b)
breadboards: 1

parts:
  X1 = DB9 Connector [package=db9]
  Part2 = Adafruit Feather RP2040 [part_number="Adafruit #4884"]
  S1 = Textile Pushbutton [part_number="TACRACPS1X0404GY "]

nets:
  N1: X1.1, Part2.GND, S1.leg1
  N2: X1.4, Part2.D5
  N3: X1.5, Part2.D10
  N4: X1.6, Part2.D11
  N5: X1.7, Part2.D6
  N6: X1.8, Part2.D9
  N7: Part2.D12, S1.leg0

custom parts:
  Adafruit Feather RP2040: A new chip means a new Feather, and the Raspberry Pi RP2040 is no exception. When we saw this chip we thought "this chip is going to be awesome when we give it the Feather Treatment" and so we did! This Feather features the RP2040, and all niceties you know and love about Feather Measures 2.0" x 0.9" x 0.28" (50.8mm x 22.8mm x 7mm) without headers soldered in Light as a (large?) feather - 5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
